# Fritzing sketch itp348_a4_Masters_Daniel_Fritzing_Diagram (saved by Fritzing 0.9.4)
breadboards: 1

parts:
  Argon1 = Particle Argon
  LED1 = LED - 5mm [color="Red (633nm)" package="5 mm [THT]"]  # not connected
  LED2 = LED - 5mm [color="Red (633nm)" package="5 mm [THT]"]
  LED3 = LED - 5mm [color="Red (633nm)" package="5 mm [THT]"]
  LED4 = LED - 5mm [color="Red (633nm)" package="5 mm [THT]"]
  LED5 = LED - 5mm [color="Red (633nm)" package="5 mm [THT]"]
  LED6 = LED - 5mm [color="Red (633nm)" package="5 mm [THT]"]
  LED7 = LED - 5mm [color="Red (633nm)" package="5 mm [THT]"]
  LED8 = LED - 5mm [color="Red (633nm)" package="5 mm [THT]"]
  LED9 = LED - 5mm [color="Red (633nm)" package="5 mm [THT]"]
  R1 = Resistor [tolerance=±5% resistance=220 package="2512 [SMD]"]
  R2 = Resistor [tolerance=±5% resistance=220 package="2512 [SMD]"]
  R3 = Resistor [tolerance=±5% resistance=220 package="2512 [SMD]"]
  R4 = Resistor [tolerance=±5% resistance=220 package="2512 [SMD]"]
  R5 = Resistor [tolerance=±5% resistance=220 package="2512 [SMD]"]
  R6 = Resistor [tolerance=±5% resistance=220 package="2512 [SMD]"]
  R7 = Resistor [tolerance=±5% resistance=220 package="2512 [SMD]"]
  R8 = Resistor [tolerance=±5% resistance=220 package="2512 [SMD]"]
  R9 = Resistor [tolerance=±5% resistance=220 package="2512 [SMD]"]
  S1 = Pushbutton [package="[THT]"]
  R10 = Resistor [tolerance=±5% resistance=220 package="0402 [SMD]"]

nets:
  N1: Argon1.3.3V, Argon1.A1, S1.Pin_1, S1.Pin_2
  N2: Argon1.GND, R1.Pin_0, R2.Pin_0, R3.Pin_0, R4.Pin_0, R5.Pin_0, R6.Pin_0, R7.Pin_0, R8.Pin_1, R9.Pin_0, R10.Pin_0
  N3: Argon1.A2, LED8.anode
  N4: Argon1.A3, LED9.anode
  N5: Argon1.D2, LED7.anode
  N6: Argon1.D3, LED6.anode
  N7: Argon1.D4, LED5.anode
  N8: Argon1.D5, LED4.anode
  N9: Argon1.D6, LED3.anode
  N10: Argon1.D7, LED2.anode
  N11: LED2.cathode, R8.Pin_0
  N12: LED3.cathode, R7.Pin_1
  N13: LED4.cathode, R6.Pin_1
  N14: LED5.cathode, R5.Pin_1
  N15: LED6.cathode, R4.Pin_1
  N16: LED7.cathode, R3.Pin_1
  N17: LED8.cathode, R2.Pin_1
  N18: LED9.cathode, R1.Pin_1
  N19: S1.Pin_3, S1.Pin_4, R10.Pin_1

notes:
  This is supposed to be a 10k ohm resistor.
  These are supposed to be 330 ohm resistors.

custom parts:
  Particle Argon: The Argon is a powerful Wi-Fi enabled development board that can act as either a standalone Wi-Fi endpoint or Wi-Fi enabled gateway for Particle Mesh networks. It is based on the Nordic nRF52840 and has built-in battery charging circuitry so it’s easy to connect a Li-Po and deploy your local network in minutes. The Argon is great for connecting existing projects to the Particle Device Cloud or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
