# Fritzing sketch itp348_a5_Masters_Daniel_FRITZING (saved by Fritzing 0.9.4)
breadboards: 2

parts:
  Argon1 = Particle Argon
  S1 = Pushbutton [package="[THT]"]
  S2 = Pushbutton [package="[THT]"]
  S3 = Pushbutton [package="[THT]"]
  R1 = Resistor [tolerance=±5% resistance=220 package=THT]
  R2 = Resistor [tolerance=±5% resistance=220 package=THT]
  R3 = Resistor [tolerance=±5% resistance=220 package=THT]
  S4 = Pushbutton [package="[SMD]"]
  R4 = Resistor [tolerance=±5% resistance=220 package=THT]
  LED1 = RGB LED (com. cathode, rbg) [package="5 mm [THT]"]
  R6 = Resistor [tolerance=±5% resistance=220 package=THT]
  R7 = Resistor [tolerance=±5% resistance=220 package=THT]
  R8 = Resistor [tolerance=±5% resistance=220 package=THT]

nets:
  N1: Argon1.MD, S1.Pin_1, S1.Pin_2, S2.Pin_1, S2.Pin_2, S3.Pin_1, S3.Pin_2, S4.Pin_1, S4.Pin_2
  N2: Argon1.A0, R1.Pin_1, R2.Pin_1, R3.Pin_0, R4.Pin_0, LED1.common_cathode
  N3: Argon1.A2, S2.Pin_3, S2.Pin_4, R2.Pin_0
  N4: Argon1.A3, S1.Pin_3, S1.Pin_4, R1.Pin_0
  N5: Argon1.A4, S3.Pin_3, S3.Pin_4, R3.Pin_1
  N6: Argon1.A5, S4.Pin_3, S4.Pin_4, R4.Pin_1
  N7: Argon1.D2, R8.Pin_1
  N8: Argon1.D3, R6.Pin_0
  N9: Argon1.D4, R7.Pin_0
  N10: LED1.red_anode, R8.Pin_0
  N11: LED1.blue_anode, R6.Pin_1
  N12: LED1.green_anode, R7.Pin_1

notes:
  The button resistors are 10k ohm
  the LED resistors are 330 ohm
  the leg that has a wire that connects to ground is the longer leg

custom parts:
  Particle Argon: The Argon is a powerful Wi-Fi enabled development board that can act as either a standalone Wi-Fi endpoint or Wi-Fi enabled gateway for Particle Mesh networks. It is based on the Nordic nRF52840 and has built-in battery charging circuitry so it’s easy to connect a Li-Po and deploy your local network in minutes. The Argon is great for connecting existing projects to the Particle Device Cloud or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
