# Fritzing sketch itp348_a7_Masters_Daniel_Fritzing (saved by Fritzing 0.9.4)
breadboards: 1

parts:
  Argon1 = Particle Argon
  S1 = Pushbutton [package="[SMD]"]
  R1 = Resistor [tolerance=±5% resistance=10k package="2512 [SMD]"]
  T1 = TMP36 Temperature Sensor [package="TO92 [THT]"]
  WeMos_D1_Mini_OLED_Shield1 = WeMos D1 Mini OLED Shield  # not connected

nets:
  N1: Argon1.3.3V, S1.Pin_1, S1.Pin_2, T1.+Vs
  GND: Argon1.GND, R1.Pin_1, T1.GND
  N2: Argon1.A5, T1.Vout
  N3: Argon1.D5, S1.Pin_3, S1.Pin_4, R1.Pin_0

notes:
  OLED, D2 is the one not plugged in

custom parts:
  Particle Argon: The Argon is a powerful Wi-Fi enabled development board that can act as either a standalone Wi-Fi endpoint or Wi-Fi enabled gateway for Particle Mesh networks. It is based on the Nordic nRF52840 and has built-in battery charging circuitry so it’s easy to connect a Li-Po and deploy your local network in minutes. The Argon is great for connecting existing projects to the Particle Device Cloud or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
