# Fritzing sketch itp348_a8_Masters_Daniel_Fritzing (saved by Fritzing 0.9.4)
breadboards: 1

parts:
  Argon1 = Particle Argon
  S1 = Pushbutton [package="[SMD]"]
  S2 = Pushbutton [package="[SMD]"]
  R1 = Resistor [tolerance=±5% resistance=10k package="2010 [SMD]"]
  R2 = Resistor [tolerance=±5% resistance=10k package="2010 [SMD]"]
  J1 = Piezo Speaker
  LED1 = LED - 5mm [color="Red (633nm)" package="5 mm [THT]"]

nets:
  N1: Argon1.3.3V, S1.Pin_1, S1.Pin_2, S2.Pin_1, S2.Pin_2
  N2: Argon1.GND, R1.Pin_1, R2.Pin_1, J1.pin1, LED1.cathode
  N3: Argon1.D2, J1.pin2
  N4: Argon1.D3, S2.Pin_3, S2.Pin_4, R2.Pin_0
  N5: Argon1.D4, S1.Pin_3, S1.Pin_4, R1.Pin_0
  N6: Argon1.D5, LED1.anode

notes:
  positive lead to D2, negative lead to ground

custom parts:
  Particle Argon: The Argon is a powerful Wi-Fi enabled development board that can act as either a standalone Wi-Fi endpoint or Wi-Fi enabled gateway for Particle Mesh networks. It is based on the Nordic nRF52840 and has built-in battery charging circuitry so it’s easy to connect a Li-Po and deploy your local network in minutes. The Argon is great for connecting existing projects to the Particle Device Cloud or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
