# Fritzing sketch itp348_finalProjectSchematic_Masters_Daniel (saved by Fritzing 0.9.4)
breadboards: 1

parts:
  Argon1 = Particle Argon
  S1 = Toggle Switch [package=THT]
  S2 = Pushbutton [package="[SMD]"]
  R1 = Resistor [tolerance=±5% resistance=10k package="0603 [SMD]"]
  J1 = Piezo Speaker
  3-Axis_Accelerometer1 = 3-Axis Accelerometer Breakout - MMA8452Q
  LED1 = smd LED [color="Red (633nm)" package="0603 [SMD]"]
  R2 = Resistor [tolerance=±5% resistance=330 package="2010 [SMD]"]
  HC-SR04_Sensor_1 = HC-SR04 Ultrasonic Distance Sensor
  U1 = LIPO-1000mAh [package=lipo-1000]  # not connected

nets:
  3.3V: Argon1.3.3V, S2.Pin_1, S2.Pin_2, 3-Axis_Accelerometer1.3.3V
  GND: Argon1.GND, S1.L2, R1.Pin_1, J1.pin1, R2.Pin_0, HC-SR04_Sensor_1.GND
  N1: Argon1.SDA, 3-Axis_Accelerometer1.SDA
  N2: Argon1.SCL, 3-Axis_Accelerometer1.SCL
  N3: Argon1.D2, HC-SR04_Sensor_1.ECHO
  N4: Argon1.D3, HC-SR04_Sensor_1.TRIG
  N5: Argon1.D4, J1.pin2
  N6: Argon1.D5, S2.Pin_3, S2.Pin_4, R1.Pin_0
  N7: Argon1.D6, LED1.anode
  N8: Argon1.VUSB, HC-SR04_Sensor_1.VCC
  N9: Argon1.EN, S1.COM
  N10: LED1.cathode, R2.Pin_1

notes:
  Ultrasonic Distance sensor is underneath breadboard.
  Lipo is underneath breadboard.

custom parts:
  Particle Argon: The Argon is a powerful Wi-Fi enabled development board that can act as either a standalone Wi-Fi endpoint or Wi-Fi enabled gateway for Particle Mesh networks. It is based on the Nordic nRF52840 and has built-in battery charging circuitry so it’s easy to connect a Li-Po and deploy your local network in minutes. The Argon is great for connecting existing projects to the Particle Device Cloud or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
